// Logisim project Lab_4.circ as structural Verilog: 1 circuit, main circuit main
// reg
module main (
  input  [3:0] in_1,
  input  LD,
  input  INC,
  input  CLR,
  input  in_5,
  input  LD_2,
  input  INC_2,
  input  CLR_2,
  input  in_9,
  input  LD_3,
  input  INC_3,
  input  CLR_3,
  input  in_13
);

  wire clock_1_out;
  wire [3:0] R1_out_6, R2_out_6, R3_out_6;

  Clock clock_1 (.out(clock_1_out));
  _4_reg R1 (.in_3(in_1), .CLK(clock_1_out), .LD(LD), .INC(INC), .CLR(CLR), .out_6(R1_out_6));
  _4_reg R2 (.in_3(in_1), .CLK(clock_1_out), .LD(LD_2), .INC(INC_2), .CLR(CLR_2), .out_6(R2_out_6));
  _4_reg R3 (.in_3(in_1), .CLK(clock_1_out), .LD(LD_3), .INC(INC_3), .CLR(CLR_3), .out_6(R3_out_6));
  // Probe on R1_out_6
  // Probe on R2_out_6
  // Probe on R3_out_6
  // Probe on in_1
  assign in_1 = in_5 ? R1_out_6 : 4'bz;  // Controlled_Buffer controlled_buffer_1
  assign in_1 = in_9 ? R2_out_6 : 4'bz;  // Controlled_Buffer controlled_buffer_2
  assign in_1 = in_13 ? R3_out_6 : 4'bz;  // Controlled_Buffer controlled_buffer_3
endmodule
