// Logisim project Project.circ as structural Verilog: 13 circuits, main circuit main
module main (
  input  [3:0] INPR
);

  wire clock_1_out, main_controller_1_ac_bus, main_controller_1_ac_clr, main_controller_1_ac_inc,
       main_controller_1_ac_load, main_controller_1_alu_add, main_controller_1_alu_and,
       main_controller_1_alu_cil, main_controller_1_alu_cir, main_controller_1_alu_cmp,
       main_controller_1_alu_ld_dr, main_controller_1_alu_ld_inpr, main_controller_1_ar_bus,
       main_controller_1_ar_inc, main_controller_1_ar_load, main_controller_1_dr_load,
       main_controller_1_ir_bus, main_controller_1_ir_load, main_controller_1_mar_bus,
       main_controller_1_mar_load, main_controller_1_pc_bus, main_controller_1_pc_inc,
       main_controller_1_pc_load;
  wire [3:0] AC_out_6, AR_out_6, DR_out_6, n4alu_1_out_14, OUTR_out_6, PC_out_6, undriven;
  wire [7:0] controlled_buffer_1_out, ram_1_data;
  wire [7:4] undriven_2;

  MAIN_Controller main_controller_1 (
    .IR_4_7(undriven_2), .MAR_LOAD(main_controller_1_mar_load), .MAR_BUS(main_controller_1_mar_bus),
    .AR_LOAD(main_controller_1_ar_load), .AR_BUS(main_controller_1_ar_bus),
    .AR_INC(main_controller_1_ar_inc), .PC_INC(main_controller_1_pc_inc), .PC_BUS(main_controller_1_pc_bus),
    .PC_LOAD(main_controller_1_pc_load), .DR_LOAD(main_controller_1_dr_load),
    .AC_LOAD(main_controller_1_ac_load), .AC_BUS(main_controller_1_ac_bus),
    .AC_CLR(main_controller_1_ac_clr), .AC_INC(main_controller_1_ac_inc),
    .IR_LOAD(main_controller_1_ir_load), .IR_BUS(main_controller_1_ir_bus),
    .ALU_AND(main_controller_1_alu_and), .ALU_ADD(main_controller_1_alu_add),
    .ALU_LD_DR(main_controller_1_alu_ld_dr), .ALU_LD_INPR(main_controller_1_alu_ld_inpr),
    .ALU_CMP(main_controller_1_alu_cmp), .ALU_CIR(main_controller_1_alu_cir),
    .ALU_CIL(main_controller_1_alu_cil));
  _4ALU u_4alu_1 (
    .AC(AC_out_6), .DR(DR_out_6), .INPR(INPR), .AND(main_controller_1_alu_and),
    .ADD(main_controller_1_alu_add), .CMA(main_controller_1_alu_cmp), .LD_DR(main_controller_1_alu_ld_dr),
    .LD_INPR(main_controller_1_alu_ld_inpr), .CIR(main_controller_1_alu_cir),
    .CIL(main_controller_1_alu_cil), .out_14(n4alu_1_out_14));  // open: cin, E_AC_0, out_15, E_AC3
  Clock clock_1 (.out(clock_1_out));
  RAM #(.addrWidth(4), .bus("separate")) ram_1 (
    .addr(AR_out_6), .din(controlled_buffer_1_out), .data(ram_1_data), .str(main_controller_1_mar_load),
    .clk(clock_1_out));  // open: sel, ld, clr
  _4Reg AR (
    .in_3(controlled_buffer_1_out[3:0]), .CLK(clock_1_out), .LD(main_controller_1_ar_load),
    .INC(main_controller_1_ar_inc), .out_6(AR_out_6));  // open: CLR
  _4Reg PC (
    .in_3(controlled_buffer_1_out[3:0]), .CLK(clock_1_out), .LD(main_controller_1_pc_load),
    .INC(main_controller_1_pc_inc), .out_6(PC_out_6));  // open: CLR
  _4Reg DR (
    .in_3(controlled_buffer_1_out[3:0]), .CLK(clock_1_out), .LD(main_controller_1_dr_load), .out_6(DR_out_6));  // open: INC, CLR
  _4Reg AC (
    .in_3(n4alu_1_out_14), .CLK(clock_1_out), .LD(main_controller_1_ac_load), .INC(main_controller_1_ac_inc),
    .CLR(main_controller_1_ac_clr), .out_6(AC_out_6));
  _8Reg IR (
    .in_2(controlled_buffer_1_out), .CLK(clock_1_out), .LD(main_controller_1_ir_load),
    .in_1({undriven_2, undriven}));  // open: INC, CLR
  _4Reg OUTR (.in_3(controlled_buffer_1_out[3:0]), .CLK(clock_1_out), .out_6(OUTR_out_6));  // open: LD, INC, CLR
  // Probe on AR_out_6
  // Probe on PC_out_6
  // Probe on DR_out_6
  // Probe on AC_out_6
  // Probe on {undriven_2, undriven}
  // Probe on OUTR_out_6
  assign controlled_buffer_1_out = main_controller_1_mar_bus ? ram_1_data : 8'bz;  // Controlled_Buffer controlled_buffer_1
  assign controlled_buffer_1_out = main_controller_1_ar_bus ? {4'b0000, AR_out_6} : 8'bz;  // Controlled_Buffer controlled_buffer_2
  assign controlled_buffer_1_out = main_controller_1_pc_bus ? {4'b0000, PC_out_6} : 8'bz;  // Controlled_Buffer controlled_buffer_3
  Controlled_Buffer #(.width(8)) controlled_buffer_4 (
    .in({4'b0000, DR_out_6}), .out(controlled_buffer_1_out));  // open: en
  assign controlled_buffer_1_out = main_controller_1_ac_bus ? {4'b0000, AC_out_6} : 8'bz;  // Controlled_Buffer controlled_buffer_5
  assign controlled_buffer_1_out = main_controller_1_ir_bus ? {undriven_2, undriven} : 8'bz;  // Controlled_Buffer controlled_buffer_6
  // Probe on controlled_buffer_1_out
endmodule

module _4Reg (
  input  INC,
  input  LD,
  input  [3:0] in_3,
  input  CLK,
  input  CLR,
  output [3:0] out_6
);

  wire and_1_out, and_2_out, and_3_out, and_4_out, and_5_out, and_6_out, and_7_out, and_8_out, and_9_out,
       and_10_out, and_11_out, and_12_out, not_1_out, not_2_out, not_3_out, not_4_out, not_5_out, not_6_out,
       or_1_out, or_2_out, or_3_out, or_4_out, or_5_out, or_6_out, or_7_out, or_8_out;

  not not_1 (not_1_out, LD);
  and and_1 (and_1_out, INC, not_1_out);
  not not_2 (not_2_out, not_1_out);
  not not_3 (not_3_out, in_3[0]);
  not not_4 (not_4_out, in_3[1]);
  not not_5 (not_5_out, in_3[2]);
  not not_6 (not_6_out, in_3[3]);
  and and_2 (and_2_out, not_2_out, in_3[0]);
  and and_3 (and_3_out, not_2_out, not_3_out);
  and and_4 (and_4_out, not_2_out, in_3[1]);
  and and_5 (and_5_out, not_2_out, not_4_out);
  and and_6 (and_6_out, not_2_out, in_3[2]);
  and and_7 (and_7_out, not_2_out, not_5_out);
  and and_8 (and_8_out, not_2_out, in_3[3]);
  and and_9 (and_9_out, not_2_out, not_6_out);
  and and_10 (and_10_out, and_1_out, out_6[0]);
  and and_11 (and_11_out, and_1_out, out_6[0], out_6[1]);
  and and_12 (and_12_out, and_1_out, out_6[0], out_6[1], out_6[2]);
  or or_1 (or_1_out, and_2_out, and_1_out);
  or or_2 (or_2_out, and_3_out, and_1_out);
  or or_3 (or_3_out, and_4_out, and_10_out);
  or or_4 (or_4_out, and_10_out, and_5_out);
  or or_5 (or_5_out, and_6_out, and_11_out);
  or or_6 (or_6_out, and_11_out, and_7_out);
  or or_7 (or_7_out, and_8_out, and_12_out);
  or or_8 (or_8_out, and_12_out, and_9_out);
  J_K_Flip_Flop j_k_ff_1 (.J(or_1_out), .clk(CLK), .K(or_2_out), .Q(out_6[0]), .reset(CLR));  // open: Qn, preset, en
  J_K_Flip_Flop j_k_ff_2 (.J(or_3_out), .clk(CLK), .K(or_4_out), .Q(out_6[1]), .reset(CLR));  // open: Qn, preset, en
  J_K_Flip_Flop j_k_ff_3 (.J(or_5_out), .clk(CLK), .K(or_6_out), .Q(out_6[2]), .reset(CLR));  // open: Qn, preset, en
  J_K_Flip_Flop j_k_ff_4 (.J(or_7_out), .clk(CLK), .K(or_8_out), .Q(out_6[3]), .reset(CLR));  // open: Qn, preset, en
endmodule

module _1ALU (
  input  INPR,
  input  DR,
  input  AC,
  input  AND,
  input  cin,
  input  ADD,
  input  CMA,
  input  LD_DR,
  input  LD_INPR,
  input  CIR,
  input  CIL,
  input  AC_i_1,
  input  AC_i_1_2,
  output cout,
  output output_AC
);

  wire add_out, adder_1_out, and_out, comp_out, Id_DR_out, Id_INPR_out, not_1_out, shl_out, shr_out;

  Adder #(.width(1)) adder_1 (.a(AC), .b(DR), .out(adder_1_out), .cin(cin), .cout(cout));
  not not_1 (not_1_out, AC);
  and u_and (and_out, AND, AC, DR);
  and u_add (add_out, ADD, adder_1_out);
  and comp (comp_out, CMA, not_1_out);
  and Id_DR (Id_DR_out, LD_DR, DR);
  and Id_INPR (Id_INPR_out, LD_INPR, INPR);
  and shl (shl_out, CIR, AC_i_1_2);
  and shr (shr_out, CIL, AC_i_1);
  or or_1 (output_AC, and_out, add_out, comp_out, Id_DR_out, Id_INPR_out, shl_out, shr_out);
endmodule

// ALU
module _4ALU (
  input  cin,
  input  [3:0] AC,
  input  E_AC_0,
  input  [3:0] DR,
  input  [3:0] INPR,
  input  AND,
  input  ADD,
  input  CMA,
  input  LD_DR,
  input  LD_INPR,
  input  CIR,
  input  CIL,
  input  E_AC3,
  output [3:0] out_14,
  output out_15
);

  wire n1alu_1_cout, n1alu_2_cout, n1alu_3_cout;

  _1ALU u_1alu_1 (
    .AND(AND), .ADD(ADD), .CMA(CMA), .LD_DR(LD_DR), .LD_INPR(LD_INPR), .CIR(CIR), .CIL(CIL), .AC_i_1(E_AC_0),
    .AC_i_1_2(AC[1]), .INPR(INPR[0]), .DR(DR[0]), .AC(AC[0]), .cin(cin), .cout(n1alu_1_cout),
    .output_AC(out_14[0]));
  _1ALU u_1alu_2 (
    .AND(AND), .ADD(ADD), .CMA(CMA), .LD_DR(LD_DR), .LD_INPR(LD_INPR), .CIR(CIR), .CIL(CIL), .AC_i_1(AC[0]),
    .AC_i_1_2(AC[2]), .INPR(INPR[1]), .DR(DR[1]), .AC(AC[1]), .cin(n1alu_1_cout), .cout(n1alu_2_cout),
    .output_AC(out_14[1]));
  _1ALU u_1alu_3 (
    .AND(AND), .ADD(ADD), .CMA(CMA), .LD_DR(LD_DR), .LD_INPR(LD_INPR), .CIR(CIR), .CIL(CIL), .AC_i_1(AC[1]),
    .AC_i_1_2(AC[3]), .INPR(INPR[2]), .DR(DR[2]), .AC(AC[2]), .cin(n1alu_2_cout), .cout(n1alu_3_cout),
    .output_AC(out_14[2]));
  _1ALU u_1alu_4 (
    .AND(AND), .ADD(ADD), .CMA(CMA), .LD_DR(LD_DR), .LD_INPR(LD_INPR), .CIR(CIR), .CIL(CIL), .AC_i_1(AC[2]),
    .AC_i_1_2(E_AC3), .INPR(INPR[3]), .DR(DR[3]), .AC(AC[3]), .cin(n1alu_3_cout), .cout(out_15),
    .output_AC(out_14[3]));
endmodule

module _8Reg (
  input  [7:0] in_1,
  input  [7:0] in_2,
  input  LD,
  input  CLR,
  input  INC,
  input  CLK
);

  _4Reg u_4reg_1 (.in_3(in_2[3:0]), .CLK(CLK), .LD(LD), .INC(INC), .CLR(CLR), .out_6(in_1[3:0]));
  _4Reg u_4reg_2 (.in_3(in_2[7:4]), .CLK(CLK), .LD(LD), .INC(INC), .CLR(CLR), .out_6(in_1[7:4]));
endmodule

module AR (
  input  D4,
  input  D5,
  input  T0,
  input  T2,
  input  T3,
  input  T4,
  output AR_BUS,
  output AR_INC,
  output AR_LD
);

  wire and_1_out, and_2_out;

  and and_1 (and_1_out, T3, D4);
  and and_2 (and_2_out, T4, D5);
  and and_3 (AR_INC, T3, D5);
  or or_1 (AR_LD, T2, T0);
  or or_2 (AR_BUS, and_1_out, and_2_out);
endmodule

module PC (
  input  D4,
  input  D5,
  input  D6,
  input  T0,
  input  T1,
  input  T3,
  input  T4,
  output PC_BUS,
  output PC_INC,
  output PC_LD
);

  wire and_1_out, and_2_out, and_3_out, and_4_out;

  and and_1 (and_1_out, D5, T3);
  and and_2 (and_2_out, D4, T3);
  and and_3 (and_3_out, D5, T4);
  and and_4 (and_4_out, D6, T3);
  or or_1 (PC_BUS, T0, and_1_out);
  or or_2 (PC_LD, and_2_out, and_3_out, and_4_out);

  assign PC_INC = T1;
endmodule

module DR (
  input  D0,
  input  D1,
  input  D2,
  input  T3,
  input  T4,
  output DR_LD
);

  wire and_1_out, and_2_out, and_3_out;

  and and_1 (and_1_out, T3, D0);
  and and_2 (and_2_out, T3, D1);
  and and_3 (and_3_out, T3, D2);
  or or_1 (DR_LD, and_1_out, and_2_out, and_3_out);
endmodule

module IR (
  input  T1,
  input  T2,
  output IR_BUS,
  output IR_LD
);


  assign IR_BUS = T2;
  assign IR_LD = T1;
endmodule

module MAR (
  input  D0,
  input  D1,
  input  D2,
  input  D3,
  input  D5,
  input  D6,
  input  T1,
  input  T3,
  output MAR_BUS,
  output MAR_LOAD
);

  wire and_1_out, and_2_out, and_3_out, and_4_out, and_5_out, and_6_out;

  and and_1 (and_1_out, D0, T3);
  and and_2 (and_2_out, D1, T3);
  and and_3 (and_3_out, D6, T3);
  and and_4 (and_4_out, D2, T3);
  and and_5 (and_5_out, D3, T3);
  and and_6 (and_6_out, D5, T3);
  or or_1 (MAR_BUS, T1, and_1_out, and_2_out, and_3_out, and_4_out);
  or or_2 (MAR_LOAD, and_5_out, and_6_out);
endmodule

module ALU_Controller (
  input  D0,
  input  D1,
  input  D2,
  input  D9,
  input  D11,
  input  D12,
  input  D13,
  input  T4,
  input  T3,
  output AND,
  output ADD,
  output LD_DR,
  output LD_INPR,
  output CMP,
  output CIR,
  output CIL
);

  and and_1 (AND, D0, T4);
  and and_2 (ADD, D1, T4);
  and and_3 (LD_DR, D2, T4);
  and and_4 (LD_INPR, D2, T4);
  and and_5 (CMP, D13, T3);
  and and_6 (CIR, D11, T3);
  and and_7 (CIL, D12, T3);
endmodule

module MAIN_Controller (
  input  [3:0] IR_4_7,
  output MAR_LOAD,
  output MAR_BUS,
  output AR_LOAD,
  output AR_BUS,
  output AR_INC,
  output PC_INC,
  output PC_BUS,
  output PC_LOAD,
  output DR_LOAD,
  output AC_LOAD,
  output AC_BUS,
  output AC_CLR,
  output AC_INC,
  output IR_LOAD,
  output IR_BUS,
  output ALU_AND,
  output ALU_ADD,
  output ALU_LD_DR,
  output ALU_LD_INPR,
  output ALU_CMP,
  output ALU_CIR,
  output ALU_CIL
);

  wire clock_1_out, decoder_1_out0, decoder_1_out1, decoder_1_out2, decoder_1_out3, decoder_1_out4,
       decoder_1_out5, decoder_1_out6, decoder_1_out7, decoder_1_out8, decoder_1_out9, decoder_1_out10,
       decoder_1_out11, decoder_1_out12, decoder_1_out13, decoder_1_out14, decoder_1_out15, decoder_2_out0,
       decoder_2_out1, decoder_2_out2, decoder_2_out3, decoder_2_out4, decoder_2_out5, decoder_2_out6,
       decoder_2_out7;
  wire [3:0] n4reg_1_out_6;

  Decoder #(.select(4)) decoder_1 (
    .out0(decoder_1_out0), .out1(decoder_1_out1), .out2(decoder_1_out2), .out3(decoder_1_out3),
    .out4(decoder_1_out4), .out5(decoder_1_out5), .out6(decoder_1_out6), .out7(decoder_1_out7),
    .out8(decoder_1_out8), .out9(decoder_1_out9), .out10(decoder_1_out10), .out11(decoder_1_out11),
    .out12(decoder_1_out12), .out13(decoder_1_out13), .out14(decoder_1_out14), .out15(decoder_1_out15),
    .sel(IR_4_7));  // open: en
  Decoder #(.select(4)) decoder_2 (
    .out0(decoder_2_out0), .out1(decoder_2_out1), .out2(decoder_2_out2), .out3(decoder_2_out3),
    .out4(decoder_2_out4), .out5(decoder_2_out5), .out6(decoder_2_out6), .out7(decoder_2_out7),
    .sel(n4reg_1_out_6));  // open: out8, out9, out10, out11, out12, out13, out14, out15, en
  Clock clock_1 (.out(clock_1_out));
  _4Reg u_4reg_1 (.CLK(clock_1_out), .out_6(n4reg_1_out_6));  // open: in_3, LD, INC, CLR
  MAR mar_1 (
    .D0(decoder_1_out0), .D1(decoder_1_out1), .D2(decoder_1_out2), .D3(decoder_1_out3), .D5(decoder_1_out5),
    .D6(decoder_1_out6), .T1(decoder_2_out1), .T3(decoder_2_out3), .MAR_BUS(MAR_BUS), .MAR_LOAD(MAR_LOAD));
  AR ar_1 (
    .D4(decoder_1_out4), .D5(decoder_1_out5), .T0(decoder_2_out0), .T2(decoder_2_out2), .T3(decoder_2_out3),
    .T4(decoder_2_out4), .AR_BUS(AR_BUS), .AR_INC(AR_INC), .AR_LD(AR_LOAD));
  PC pc_1 (
    .D4(decoder_1_out4), .D5(decoder_1_out5), .D6(decoder_1_out6), .T0(decoder_2_out0), .T1(decoder_2_out1),
    .T3(decoder_2_out3), .T4(decoder_2_out4), .PC_BUS(PC_BUS), .PC_INC(PC_INC), .PC_LD(PC_LOAD));
  DR dr_1 (
    .D0(decoder_1_out0), .D1(decoder_1_out1), .D2(decoder_1_out2), .T3(decoder_2_out3), .T4(decoder_2_out4),
    .DR_LD(DR_LOAD));
  AC ac_1 (
    .D0(decoder_1_out0), .D1(decoder_1_out1), .D2(decoder_1_out2), .D3(decoder_1_out3), .D7(decoder_1_out7),
    .D9(decoder_1_out9), .D10(decoder_1_out10), .D11(decoder_1_out11), .D12(decoder_1_out12),
    .D13(decoder_1_out13), .D14(decoder_1_out14), .D15(decoder_1_out15), .T3(decoder_2_out3),
    .T4(decoder_2_out4), .AC_LD(AC_LOAD), .AC_BUS(AC_BUS), .AC_CLR(AC_CLR), .AC_INC(AC_INC));
  IR ir_1 (.T1(decoder_2_out1), .T2(decoder_2_out2), .IR_BUS(IR_BUS), .IR_LD(IR_LOAD));
  ALU_Controller alu_controller_1 (
    .D0(decoder_1_out0), .D1(decoder_1_out1), .D2(decoder_1_out2), .D9(decoder_1_out9),
    .D11(decoder_1_out11), .D12(decoder_1_out12), .D13(decoder_1_out13), .T4(decoder_2_out4),
    .T3(decoder_2_out3), .AND(ALU_AND), .ADD(ALU_ADD), .LD_DR(ALU_LD_DR), .LD_INPR(ALU_LD_INPR),
    .CMP(ALU_CMP), .CIR(ALU_CIR), .CIL(ALU_CIL));

  // Notes on the sheet:
  //   D
  //   T
endmodule

module AC (
  input  D0,
  input  D1,
  input  D2,
  input  D3,
  input  D7,
  input  D9,
  input  D10,
  input  D11,
  input  D12,
  input  D13,
  input  D14,
  input  D15,
  input  T3,
  input  T4,
  output AC_LD,
  output AC_BUS,
  output AC_CLR,
  output AC_INC
);

  wire and_1_out, and_2_out, and_3_out, and_4_out, and_5_out, and_6_out, and_7_out, and_8_out, and_9_out;

  and and_1 (and_1_out, T4, D0);
  and and_2 (and_2_out, D1, T4);
  and and_3 (and_3_out, D2, T4);
  and and_4 (and_4_out, D11, T3);
  and and_5 (and_5_out, D12, T3);
  and and_6 (and_6_out, D13, T3);
  and and_7 (and_7_out, D9, T3);
  and and_8 (and_8_out, D3, T3);
  and and_9 (and_9_out, D14, T3);
  or or_1 (AC_BUS, and_8_out, and_9_out);
  and and_10 (AC_CLR, D7, T3);
  and and_11 (AC_INC, D10, T3);
  or or_2 (AC_LD, and_1_out, and_2_out, and_3_out, and_4_out, and_5_out, and_6_out, and_7_out);
endmodule
